// Logisim project EP01.circ as structural Verilog: 5 circuits, main circuit Meia-soma
// HA
module Meia_soma (
  input  a,
  input  b,
  output soma,
  output carry_out
);

  xor xor_1 (soma, a, b);
  and and_1 (carry_out, b, a);
endmodule

// FA
module Somador_completo (
  input  a,
  input  b,
  input  carry_in,
  output soma,
  output carry_out
);

  wire meia_soma_1_carry_out, meia_soma_1_soma, meia_soma_2_carry_out;

  Meia_soma meia_soma_1 (.a(a), .b(b), .soma(meia_soma_1_soma), .carry_out(meia_soma_1_carry_out));
  or or_1 (carry_out, meia_soma_1_carry_out, meia_soma_2_carry_out);
  Meia_soma meia_soma_2 (.a(meia_soma_1_soma), .b(carry_in), .soma(soma), .carry_out(meia_soma_2_carry_out));
endmodule

// Soma
module Somador_4bits (
  input  carry_in,
  input  a0,
  input  b0,
  input  a1,
  input  b1,
  input  a2,
  input  b2,
  input  a3,
  input  b3,
  output s0,
  output s1,
  output s2,
  output s3,
  output overflow,
  output carry_out
);

  wire somador_completo_1_carry_out, somador_completo_2_carry_out, somador_completo_3_carry_out;

  Somador_completo somador_completo_1 (
    .a(a0), .b(b0), .soma(s0), .carry_in(carry_in), .carry_out(somador_completo_1_carry_out));
  Somador_completo somador_completo_2 (
    .a(a1), .b(b1), .soma(s1), .carry_in(somador_completo_1_carry_out),
    .carry_out(somador_completo_2_carry_out));
  Somador_completo somador_completo_3 (
    .a(a2), .b(b2), .soma(s2), .carry_in(somador_completo_2_carry_out),
    .carry_out(somador_completo_3_carry_out));
  Somador_completo somador_completo_4 (
    .a(a3), .b(b3), .soma(s3), .carry_in(somador_completo_3_carry_out), .carry_out(carry_out));
  xor xor_1 (overflow, somador_completo_3_carry_out, carry_out);
endmodule

// Decodifica
module Decodificador (
  input  a0,
  input  a1,
  input  a2,
  input  a3,
  output s0,
  output s1,
  output s2,
  output s3,
  output s4,
  output s5,
  output s6,
  output s7
);

  wire and_1_out, and_2_out, and_3_out, and_4_out, and_5_out, and_6_out, and_7_out, and_8_out, and_9_out,
       and_10_out, and_11_out, and_12_out, and_13_out, and_14_out, and_15_out, and_16_out, and_17_out,
       and_18_out, and_19_out, and_20_out, and_21_out, and_22_out, and_23_out, and_24_out, and_25_out,
       and_26_out, and_27_out, and_28_out, and_29_out, and_30_out, and_31_out, and_32_out, and_33_out,
       and_34_out, and_35_out, not_1_out, not_2_out, not_3_out, not_4_out, not_5_out, not_6_out, not_7_out,
       not_8_out, not_9_out, not_10_out, not_11_out, not_12_out, not_13_out, not_14_out, not_15_out,
       not_16_out, not_17_out, not_18_out, not_19_out, not_20_out, not_21_out, not_22_out, not_23_out,
       not_24_out, not_25_out, not_26_out, not_27_out, not_28_out, not_29_out, not_30_out, not_31_out,
       not_32_out, not_33_out, not_34_out, not_35_out, not_36_out, not_37_out, not_38_out, not_39_out,
       not_40_out, not_41_out, not_42_out, not_43_out;

  not not_1 (not_1_out, a0);
  and and_1 (and_1_out, not_1_out, not_2_out);
  not not_2 (not_2_out, a1);
  not not_3 (not_3_out, a0);
  not not_4 (not_4_out, a2);
  and and_2 (and_2_out, not_3_out, not_4_out, not_5_out);
  not not_5 (not_5_out, a3);
  not not_6 (not_6_out, a1);
  and and_3 (and_3_out, not_6_out, not_7_out);
  not not_7 (not_7_out, a3);
  not not_8 (not_8_out, a0);
  and and_4 (and_4_out, not_8_out, a2, a3);
  and and_5 (and_5_out, a0, not_9_out, a3);
  not not_9 (not_9_out, a2);
  not not_10 (not_10_out, a1);
  and and_6 (and_6_out, not_10_out, not_11_out);
  not not_11 (not_11_out, a3);
  not not_12 (not_12_out, a0);
  and and_7 (and_7_out, not_12_out, a2);
  not not_13 (not_13_out, a0);
  and and_8 (and_8_out, not_13_out, a1, a3);
  and and_9 (and_9_out, a1, a2);
  not not_14 (not_14_out, a1);
  and and_10 (and_10_out, a0, not_14_out, not_15_out);
  not not_15 (not_15_out, a2);
  and and_11 (and_11_out, a0, not_16_out);
  not not_16 (not_16_out, a3);
  not not_17 (not_17_out, a2);
  and and_12 (and_12_out, not_17_out, not_18_out);
  not not_18 (not_18_out, a3);
  not not_19 (not_19_out, a0);
  and and_13 (and_13_out, not_19_out, a1, not_20_out);
  not not_20 (not_20_out, a2);
  and and_14 (and_14_out, a1, not_21_out);
  not not_21 (not_21_out, a3);
  and and_15 (and_15_out, a0, not_22_out);
  not not_22 (not_22_out, a1);
  and and_16 (and_16_out, a0, a2);
  not not_23 (not_23_out, a1);
  and and_17 (and_17_out, not_23_out, a2);
  and and_18 (and_18_out, a2, not_24_out);
  not not_24 (not_24_out, a3);
  not not_25 (not_25_out, a0);
  and and_19 (and_19_out, not_25_out, a1, not_26_out);
  not not_26 (not_26_out, a2);
  and and_20 (and_20_out, a0, not_27_out);
  not not_27 (not_27_out, a1);
  and and_21 (and_21_out, a0, a3);
  not not_28 (not_28_out, a1);
  and and_22 (and_22_out, not_28_out, not_29_out);
  not not_29 (not_29_out, a3);
  and and_23 (and_23_out, a2, not_30_out);
  not not_30 (not_30_out, a3);
  and and_24 (and_24_out, a0, a2);
  and and_25 (and_25_out, a0, a1);
  not not_31 (not_31_out, a0);
  and and_26 (and_26_out, not_31_out, not_32_out, not_33_out);
  not not_32 (not_32_out, a1);
  not not_33 (not_33_out, a3);
  not not_34 (not_34_out, a1);
  and and_27 (and_27_out, not_34_out, a2, a3);
  and and_28 (and_28_out, a1, not_35_out, a3);
  not not_35 (not_35_out, a2);
  and and_29 (and_29_out, a1, a2, not_36_out);
  not not_36 (not_36_out, a3);
  and and_30 (and_30_out, a0, not_37_out);
  not not_37 (not_37_out, a2);
  not not_38 (not_38_out, a0);
  and and_31 (and_31_out, not_38_out, not_39_out);
  not not_39 (not_39_out, a2);
  not not_40 (not_40_out, a0);
  and and_32 (and_32_out, not_40_out, a3);
  not not_41 (not_41_out, a2);
  and and_33 (and_33_out, not_41_out, a3);
  not not_42 (not_42_out, a0);
  and and_34 (and_34_out, not_42_out, a1);
  and and_35 (and_35_out, a0, not_43_out);
  not not_43 (not_43_out, a1);
  or or_1 (s0, and_1_out, and_2_out, and_3_out, and_4_out, and_5_out);
  or or_2 (s2, and_12_out, and_13_out, and_14_out, and_15_out, and_16_out);
  or or_3 (s3, and_17_out, and_18_out, and_19_out, and_20_out, and_21_out);
  or or_4 (s4, and_22_out, and_23_out, and_24_out, and_25_out);
  or or_5 (s5, and_26_out, and_27_out, and_28_out, and_29_out, and_30_out);
  or or_6 (s6, and_31_out, and_32_out, and_33_out, and_34_out, and_35_out);
  or or_7 (s1, and_6_out, and_7_out, and_8_out, and_9_out, and_10_out, and_11_out);

  assign s7 = 1'b0;
endmodule

module Calculadora (
  input  carry_in,
  input  [3:0] a,
  input  [3:0] b,
  output [3:0] s,
  output carry_out,
  output overflow
);

  wire decodificador_1_s0, decodificador_1_s1, decodificador_1_s2, decodificador_1_s3, decodificador_1_s4,
       decodificador_1_s5, decodificador_1_s6, decodificador_1_s7, decodificador_2_s0, decodificador_2_s1,
       decodificador_2_s2, decodificador_2_s3, decodificador_2_s4, decodificador_2_s5, decodificador_2_s6,
       decodificador_2_s7, decodificador_3_s0, decodificador_3_s1, decodificador_3_s2, decodificador_3_s3,
       decodificador_3_s4, decodificador_3_s5, decodificador_3_s6, decodificador_3_s7;

  Decodificador decodificador_1 (
    .a0(a[3]), .a1(a[2]), .a2(a[1]), .a3(a[0]), .s0(decodificador_1_s0), .s1(decodificador_1_s1),
    .s2(decodificador_1_s2), .s3(decodificador_1_s3), .s4(decodificador_1_s4), .s5(decodificador_1_s5),
    .s6(decodificador_1_s6), .s7(decodificador_1_s7));
  Somador_4bits somador_4bits_1 (
    .a0(a[0]), .b0(b[0]), .a1(a[1]), .b1(b[1]), .a2(a[2]), .b2(b[2]), .s0(s[0]), .s1(s[1]), .s2(s[2]),
    .carry_in(carry_in), .carry_out(carry_out), .a3(a[3]), .b3(b[3]), .s3(s[3]), .overflow(overflow));
  Decodificador decodificador_2 (
    .a0(b[3]), .a1(b[2]), .a2(b[1]), .a3(b[0]), .s0(decodificador_2_s0), .s1(decodificador_2_s1),
    .s2(decodificador_2_s2), .s3(decodificador_2_s3), .s4(decodificador_2_s4), .s5(decodificador_2_s5),
    .s6(decodificador_2_s6), .s7(decodificador_2_s7));
  _7_Segment_Display u_7_segment_display_1 (
    .g(decodificador_1_s3), .f(decodificador_1_s2), .a(decodificador_1_s1), .b(decodificador_1_s0),
    .e(decodificador_1_s4), .d(decodificador_1_s5), .c(decodificador_1_s6), .dp(decodificador_1_s7));
  _7_Segment_Display u_7_segment_display_2 (
    .g(decodificador_2_s3), .f(decodificador_2_s2), .a(decodificador_2_s1), .b(decodificador_2_s0),
    .e(decodificador_2_s4), .d(decodificador_2_s5), .c(decodificador_2_s6), .dp(decodificador_2_s7));
  Decodificador decodificador_3 (
    .a0(s[3]), .a1(s[2]), .a2(s[1]), .a3(s[0]), .s0(decodificador_3_s0), .s1(decodificador_3_s1),
    .s2(decodificador_3_s2), .s3(decodificador_3_s3), .s4(decodificador_3_s4), .s5(decodificador_3_s5),
    .s6(decodificador_3_s6), .s7(decodificador_3_s7));
  _7_Segment_Display u_7_segment_display_3 (
    .g(decodificador_3_s3), .f(decodificador_3_s2), .a(decodificador_3_s1), .b(decodificador_3_s0),
    .e(decodificador_3_s4), .d(decodificador_3_s5), .c(decodificador_3_s6), .dp(decodificador_3_s7));
endmodule
