// Logisim project EP02.circ as structural Verilog: 2 circuits, main circuit ULA_1bit
// ULA
module ULA_1bit (
  input  b_invert,
  input  carry_in,
  input  [1:0] op_code,
  input  a,
  input  b,
  output result,
  output carry_out
);

  wire adder_1_out, and_1_out, multiplexer_1_out, not_1_out, not_2_out, or_1_out;

  Multiplexer #(.enable("false")) multiplexer_1 (.in0(b), .in1(not_1_out), .out(multiplexer_1_out), .sel(b_invert));
  not not_1 (not_1_out, b);
  and and_1 (and_1_out, a, multiplexer_1_out);
  or or_1 (or_1_out, a, multiplexer_1_out);
  not not_2 (not_2_out, a);
  Adder #(.width(1)) adder_1 (.a(a), .b(multiplexer_1_out), .out(adder_1_out), .cin(carry_in), .cout(carry_out));
  Multiplexer #(.select(2), .enable("false")) multiplexer_2 (
    .in0(and_1_out), .in1(or_1_out), .in2(not_2_out), .in3(adder_1_out), .out(result), .sel(op_code));
endmodule

module ULA_4bits (
  input  [3:0] B,
  input  [3:0] A,
  input  b_invert,
  input  [1:0] op_code,
  output [3:0] S,
  output carry_out
);

  wire ula_1bit_1_carry_out, ula_1bit_2_carry_out, ula_1bit_3_carry_out;

  ULA_1bit ula_1bit_1 (
    .a(A[0]), .b(B[0]), .b_invert(b_invert), .carry_in(b_invert), .op_code(op_code),
    .carry_out(ula_1bit_1_carry_out), .result(S[0]));
  ULA_1bit ula_1bit_2 (
    .a(A[1]), .b(B[1]), .b_invert(b_invert), .carry_in(ula_1bit_1_carry_out), .op_code(op_code),
    .carry_out(ula_1bit_2_carry_out), .result(S[1]));
  ULA_1bit ula_1bit_3 (
    .a(A[2]), .b(B[2]), .b_invert(b_invert), .carry_in(ula_1bit_2_carry_out), .op_code(op_code),
    .carry_out(ula_1bit_3_carry_out), .result(S[2]));
  ULA_1bit ula_1bit_4 (
    .a(A[3]), .b(B[3]), .b_invert(b_invert), .carry_in(ula_1bit_3_carry_out), .op_code(op_code),
    .carry_out(carry_out), .result(S[3]));
endmodule
